// Logisim project LFSR.circ as structural Verilog
module mainnofpga (
  input  CLK100MHZ,
  input  RESET,
  input  START,
  input  MODE
);

  wire controlunit_1_ldcu, controlunit_1_rstcu_lfsr, LENLOOP_out, lfsr4_5bit_1_stopcu;
  wire [3:0] binarytobcd_1_p3, binarytobcd_1_p4, binarytobcd_2_p3, binarytobcd_2_p4;
  wire [4:0] buttonhandler_1_looplenghtout, lfsr4_5bit_1_q, lfsr_translator_1_nq;
  wire [6:0] bcdtosevensegmentnegativelogic_1_segment_output,
       bcdtosevensegmentnegativelogic_2_segment_output, bcdtosevensegmentnegativelogic_3_segment_output,
       bcdtosevensegmentnegativelogic_4_segment_output;

  Button LENLOOP (.out(LENLOOP_out));
  ControlUnit controlunit_1 (
    .clkCU(CLK100MHZ), .RSTCU(RESET), .STRTCU(START), .STPCU(lfsr4_5bit_1_stopcu), .LDCU(controlunit_1_ldcu),
    .RSTCU_lfsr(controlunit_1_rstcu_lfsr));
  ButtonHandler buttonhandler_1 (
    .clk(CLK100MHZ), .reset(RESET), .button(LENLOOP_out), .looplenghtout(buttonhandler_1_looplenghtout));
  LFSR_Translator lfsr_translator_1 (.CLK(CLK100MHZ), .MODE(MODE), .Q(lfsr4_5bit_1_q), .NQ(lfsr_translator_1_nq));
  LFSR4_5bit lfsr4_5bit_1 (
    .CLK(CLK100MHZ), .RESET(controlunit_1_rstcu_lfsr), .MODE(MODE), .LOAD(controlunit_1_ldcu),
    .N(buttonhandler_1_looplenghtout), .Q(lfsr4_5bit_1_q), .STOPCU(lfsr4_5bit_1_stopcu));
  // BinaryToBCD binarytobcd_1: pin names not known; wires that end beside it: CLK100MHZ, buttonhandler_1_looplenghtout, binarytobcd_1_p3, binarytobcd_1_p4
  // BinaryToBCD binarytobcd_2: pin names not known; wires that end beside it: CLK100MHZ, lfsr_translator_1_nq, binarytobcd_2_p3, binarytobcd_2_p4
  BCDToSevenSegmentNegativeLogic bcdtosevensegmentnegativelogic_1 (
    .bcd_input(binarytobcd_2_p4), .segment_output(bcdtosevensegmentnegativelogic_1_segment_output));
  BCDToSevenSegmentNegativeLogic bcdtosevensegmentnegativelogic_2 (
    .bcd_input(binarytobcd_2_p3), .segment_output(bcdtosevensegmentnegativelogic_2_segment_output));
  BCDToSevenSegmentNegativeLogic bcdtosevensegmentnegativelogic_3 (
    .bcd_input(binarytobcd_1_p4), .segment_output(bcdtosevensegmentnegativelogic_3_segment_output));
  BCDToSevenSegmentNegativeLogic bcdtosevensegmentnegativelogic_4 (
    .bcd_input(binarytobcd_1_p3), .segment_output(bcdtosevensegmentnegativelogic_4_segment_output));
  _7_Segment_Display u_7_segment_display_1 (
    .g(bcdtosevensegmentnegativelogic_2_segment_output[6]),
    .f(bcdtosevensegmentnegativelogic_2_segment_output[5]),
    .a(bcdtosevensegmentnegativelogic_2_segment_output[0]),
    .b(bcdtosevensegmentnegativelogic_2_segment_output[1]),
    .e(bcdtosevensegmentnegativelogic_2_segment_output[4]),
    .d(bcdtosevensegmentnegativelogic_2_segment_output[3]),
    .c(bcdtosevensegmentnegativelogic_2_segment_output[2]));  // open: dp
  _7_Segment_Display u_7_segment_display_2 (
    .g(bcdtosevensegmentnegativelogic_1_segment_output[6]),
    .f(bcdtosevensegmentnegativelogic_1_segment_output[5]),
    .a(bcdtosevensegmentnegativelogic_1_segment_output[0]),
    .b(bcdtosevensegmentnegativelogic_1_segment_output[1]),
    .e(bcdtosevensegmentnegativelogic_1_segment_output[4]),
    .d(bcdtosevensegmentnegativelogic_1_segment_output[3]),
    .c(bcdtosevensegmentnegativelogic_1_segment_output[2]));  // open: dp
  _7_Segment_Display u_7_segment_display_3 (
    .g(bcdtosevensegmentnegativelogic_4_segment_output[6]),
    .f(bcdtosevensegmentnegativelogic_4_segment_output[5]),
    .a(bcdtosevensegmentnegativelogic_4_segment_output[0]),
    .b(bcdtosevensegmentnegativelogic_4_segment_output[1]),
    .e(bcdtosevensegmentnegativelogic_4_segment_output[4]),
    .d(bcdtosevensegmentnegativelogic_4_segment_output[3]),
    .c(bcdtosevensegmentnegativelogic_4_segment_output[2]));  // open: dp
  _7_Segment_Display u_7_segment_display_4 (
    .g(bcdtosevensegmentnegativelogic_3_segment_output[6]),
    .f(bcdtosevensegmentnegativelogic_3_segment_output[5]),
    .a(bcdtosevensegmentnegativelogic_3_segment_output[0]),
    .b(bcdtosevensegmentnegativelogic_3_segment_output[1]),
    .e(bcdtosevensegmentnegativelogic_3_segment_output[4]),
    .d(bcdtosevensegmentnegativelogic_3_segment_output[3]),
    .c(bcdtosevensegmentnegativelogic_3_segment_output[2]));  // open: dp
endmodule

module mainfpga (
  input  CLK100MHZ,
  input  RESET,
  input  START,
  input  MODE,
  output [6:0] CATOD,
  output [3:0] ANOD
);

  wire controlunit_1_ldcu, controlunit_1_rstcu_lfsr, LENLOOP_out, lfsr4_5bit_1_stopcu;
  wire [3:0] binarytobcd_1_bcd_tens, binarytobcd_1_bcd_units, binarytobcd_2_bcd_tens, binarytobcd_2_bcd_units;
  wire [4:0] buttonhandler_1_looplenghtout, divisor_frecv200hz_1_clk_out_200hz, lfsr4_5bit_1_q,
       lfsr_translator_1_nq;

  Button LENLOOP (.out(LENLOOP_out));
  divisor_frecv200hz divisor_frecv200hz_1 (
    .clk_in_100mhz(CLK100MHZ), .clk_out_200hz(divisor_frecv200hz_1_clk_out_200hz[0]));
  ControlUnit controlunit_1 (
    .clkCU(divisor_frecv200hz_1_clk_out_200hz[0]), .RSTCU(RESET), .STRTCU(START),
    .STPCU(lfsr4_5bit_1_stopcu), .LDCU(controlunit_1_ldcu), .RSTCU_lfsr(controlunit_1_rstcu_lfsr));
  ButtonHandler buttonhandler_1 (
    .clk(divisor_frecv200hz_1_clk_out_200hz[0]), .reset(RESET), .button(LENLOOP_out),
    .looplenghtout(buttonhandler_1_looplenghtout));
  LFSR_Translator lfsr_translator_1 (
    .CLK(divisor_frecv200hz_1_clk_out_200hz[0]), .MODE(MODE), .Q(lfsr4_5bit_1_q), .NQ(lfsr_translator_1_nq));
  LFSR4_5bit lfsr4_5bit_1 (
    .CLK(divisor_frecv200hz_1_clk_out_200hz[0]), .RESET(controlunit_1_rstcu_lfsr), .MODE(MODE),
    .LOAD(controlunit_1_ldcu), .N(buttonhandler_1_looplenghtout), .Q(lfsr4_5bit_1_q),
    .STOPCU(lfsr4_5bit_1_stopcu));
  BinaryToBCD binarytobcd_1 (
    .binary_input(divisor_frecv200hz_1_clk_out_200hz), .bcd_tens(binarytobcd_1_bcd_tens),
    .bcd_units(binarytobcd_1_bcd_units));
  BinaryToBCD binarytobcd_2 (
    .binary_input(divisor_frecv200hz_1_clk_out_200hz), .bcd_tens(binarytobcd_2_bcd_tens),
    .bcd_units(binarytobcd_2_bcd_units));
  Display display_1 (
    .clk(divisor_frecv200hz_1_clk_out_200hz[0]), .looplen_unit(binarytobcd_2_bcd_units),
    .looplen_tens(binarytobcd_2_bcd_tens), .lfsrout_unit(binarytobcd_1_bcd_units),
    .lfsrout_tens(binarytobcd_1_bcd_tens), .cat(CATOD), .an(ANOD));
  // Pins of 1 and 5 bits meet at divisor_frecv200hz_1_clk_out_200hz
endmodule

module mainDesignLFSRfpga (
  input  CLK100MHZ,
  input  START_SW,
  input  MODE_SW,
  output [6:0] CAT,
  output [3:0] AN
);

  wire LL_B_out, RST_B_out;

  Button RST_B (.out(RST_B_out));
  Button LL_B (.out(LL_B_out));
  MainDesignLFSR maindesignlfsr_1 (
    .CLK(CLK100MHZ), .START(START_SW), .MODE(MODE_SW), .RESET(RST_B_out), .LENLOOP(LL_B_out), .CATOD(CAT),
    .ANOD(AN));
endmodule

// VHDL entity divisor_frecv200hz, as the project stores it:
library IEEE;
use IEEE.STD_LOGIC_1164.ALL;
entity divisor_frecv200hz is
    Port (
        clk_in_100mhz : in  STD_LOGIC;
        clk_out_200hz: out STD_LOGIC
    );
end divisor_frecv200hz;
architecture Behavioral of divisor_frecv200hz is
    signal temporal: STD_LOGIC;
    signal counter : integer range 0 to 124999 := 0;
begin
    frequency_divider: process (clk_in_100mhz) begin
        if rising_edge(clk_in_100mhz) then
            if (counter = 124999) then
                temporal <= NOT(temporal);
                counter <= 0;
            else
                counter <= counter + 1;
            end if;
         end if;
    end process;
    clk_out_200hz <= temporal;
end Behavioral;

// VHDL entity ButtonHandler, as the project stores it:
LIBRARY ieee;
USE ieee.std_logic_1164.all;
USE ieee.numeric_std.all;
ENTITY ButtonHandler IS
  PORT (
    clk: IN std_logic;
    reset: IN std_logic;
    button: IN std_logic; --give loop lenghloop
    looplenghtout: OUT std_logic_vector(4 DOWNTO 0)
  );
END ENTITY ButtonHandler;
ARCHITECTURE Behavioral OF ButtonHandler IS
  SIGNAL count: integer := 0;
  SIGNAL button_state, button_prev: std_logic := '0';
  SIGNAL debounce_counter: integer := 0;
  SIGNAL debounce_limit: integer := 2; -- Adjust this value based on your clock frequency and desired debounce time
BEGIN
  PROCESS (clk)
  BEGIN
    IF rising_edge(clk) THEN
      IF reset = '1' THEN
        count <= 0;
        button_state <= '0';
        button_prev <= '0';
        debounce_counter <= 0;
      ELSE
        button_prev <= button_state;
        button_state <= button;
        IF button_state = '1' AND button_prev = '0' THEN
          debounce_counter <= debounce_limit;
          count <= count + 1;
          IF count > 31 THEN
            count <= 1;
          END IF;
        ELSIF debounce_counter > 0 THEN
          debounce_counter <= debounce_counter - 1;
        END IF;
      END IF;
    END IF;
  END PROCESS;
  looplenghtout <= std_logic_vector(to_unsigned(count, looplenghtout'length));
END ARCHITECTURE Behavioral;

// VHDL entity BinaryToBCD, as the project stores it:
LIBRARY ieee;
USE ieee.std_logic_1164.all;
USE ieee.numeric_std.all;
ENTITY BinaryToBCD IS
  PORT (
    binary_input: IN std_logic_vector(4 DOWNTO 0);
    bcd_tens: OUT std_logic_vector(3 DOWNTO 0);
    bcd_units: OUT std_logic_vector(3 DOWNTO 0)
  );
END ENTITY BinaryToBCD_outdated;
ARCHITECTURE Behavioral OF BinaryToBCD_outdated IS
BEGIN
  PROCESS (binary_input)
    VARIABLE decimal_value: integer;
  BEGIN
    decimal_value := to_integer(unsigned(binary_input));
    bcd_tens <= std_logic_vector(to_unsigned(decimal_value / 10, bcd_tens'length));
    bcd_units <= std_logic_vector(to_unsigned(decimal_value mod 10, bcd_units'length));
  END PROCESS;
END ARCHITECTURE Behavioral;

// VHDL entity BCDToSevenSegmentNegativeLogic, as the project stores it:
LIBRARY ieee;
USE ieee.std_logic_1164.all;
ENTITY BCDToSevenSegmentNegativeLogic IS
  PORT (
    bcd_input: IN std_logic_vector(3 DOWNTO 0);
    segment_output: OUT std_logic_vector(6 DOWNTO 0)
  );
END ENTITY BCDToSevenSegmentNegativeLogic;
ARCHITECTURE Behavioral OF BCDToSevenSegmentNegativeLogic IS
BEGIN
  PROCESS (bcd_input)
  BEGIN
    CASE bcd_input IS
      WHEN "0000" => segment_output <= "0111111"; -- 0
      WHEN "0001" => segment_output <= "0000110"; -- 1
      WHEN "0010" => segment_output <= "1011011"; -- 2
      WHEN "0011" => segment_output <= "1001111"; -- 3
      WHEN "0100" => segment_output <= "1100110"; -- 4
      WHEN "0101" => segment_output <= "1101101"; -- 5
      WHEN "0110" => segment_output <= "1111101"; -- 6
      WHEN "0111" => segment_output <= "0000111"; -- 7
      WHEN "1000" => segment_output <= "1111111"; -- 8
      WHEN "1001" => segment_output <= "1101111"; -- 9
      WHEN OTHERS => segment_output <= "0000000"; -- Error (all segments on)
    END CASE;
  END PROCESS;
END ARCHITECTURE Behavioral;

// VHDL entity ControlUnit, as the project stores it:
library IEEE;
use IEEE.STD_LOGIC_1164.ALL;
use IEEE.STD_LOGIC_ARITH.ALL;
use IEEE.STD_LOGIC_UNSIGNED.ALL;

entity ControlUnit is
    Port (
        clkCU : in STD_LOGIC;
        RSTCU : in STD_LOGIC;
        STRTCU : in STD_LOGIC;
        STPCU : in STD_LOGIC;
        LDCU : out STD_LOGIC;
        RSTCU_lfsr : out STD_LOGIC
    );
end ControlUnit;

architecture behavioral of ControlUnit is
    -- Define the states
    type state_type is (state_A, state_B, state_C, state_D);
    signal current_state, next_state: state_type;

    -- Internal signal for ENCU
    signal internal_ENCU : STD_LOGIC;

begin
    -- State transition process
    process(clkCU, RSTCU)
    begin
        if RSTCU = '1' then
            current_state <= state_A;
        elsif rising_edge(clkCU) then
            current_state <= next_state;
        end if;
    end process;

    -- Next state logic process
    process(current_state, STRTCU, STPCU)
    begin
        case current_state is
            when state_A =>
                if STRTCU = '1' then
                    next_state <= state_B;
                else
                    next_state <= state_A;
                end if;

            when state_B =>
                next_state <= state_C;

            when state_C =>
                if STPCU = '1' then
                    next_state <= state_D;
                else
                    next_state <= state_C;
                end if;

            when state_D =>
                next_state <= state_A;

            when others =>
                next_state <= state_A;
        end case;
    end process;

    -- Output logic process
    process(current_state)
    begin
        case current_state is
            when state_A =>
                internal_ENCU <= '0';
                LDCU <= '0';
                RSTCU_lfsr <= '0';
            when state_B =>
                internal_ENCU <= '0';
                LDCU <= '1';
                RSTCU_lfsr <= '0';
            when state_C =>
                internal_ENCU <= '1';
                LDCU <= '0';
                RSTCU_lfsr <= '0';
            when state_D =>
                internal_ENCU <= '0';
                LDCU <= '0';
                RSTCU_lfsr <= '1';
            when others =>
                internal_ENCU <= '0';
                LDCU <= '0';
                RSTCU_lfsr <= '0';
        end case;
    end process;
end behavioral;

// VHDL entity LFSR4_5bit, as the project stores it:
library IEEE;
use IEEE.STD_LOGIC_1164.ALL;
use ieee.numeric_std.all;
use IEEE.STD_LOGIC_UNSIGNED.ALL;

entity LFSR4_5bit is
    Port ( CLK : in STD_LOGIC;
           RESET : in STD_LOGIC;
           MODE : in STD_LOGIC;
           LOAD : in STD_LOGIC;
           N : in STD_LOGIC_VECTOR (4 downto 0);
           Q : out STD_LOGIC_VECTOR (4 downto 0);
           STOPCU : out STD_LOGIC);
end LFSR4_5bit;

architecture Behavioral of LFSR4_5bit is
    type state_type is (IDLE, generating, waiting);
    signal state : state_type := IDLE;
    signal reg : INTEGER := 0;
    signal count : INTEGER := 0;
    signal num_generated : INTEGER := 0;
    signal wait_count : INTEGER := 0;
    
    constant f_clk : INTEGER := 2; -- Adjust this value according to your clock frequency (200 Hz in this case)
    constant delay_cycles : INTEGER := 2 * f_clk;

    type int_array is array (natural range <>) of integer;
    constant values_4bit : int_array := (
        0, 8, 12, 14, 7, 10, 13, 11, 9, 4, 6, 5, 3, 2, 1
    );
    constant values_5bit : int_array := (
        0, 16, 24, 28, 30, 23, 22, 19, 18, 15, 14, 29, 13, 6, 5, 26,
        3, 11, 10, 17, 16, 20, 25, 6, 24, 21, 31, 23, 22, 7, 19, 18
    );

begin
    process (CLK, RESET)
    begin
        if RESET = '1' then
            reg <= 0;
            count <= 0;
            num_generated <= 0;
            wait_count <= 0;
            state <= IDLE;
            STOPCU <= '0';
        elsif rising_edge(CLK) then
            case state is
                when IDLE =>
                    if LOAD = '1' then
                        reg <= 0;
                        count <= 0;
                        num_generated <= 0;
                        state <= generating;
                    end if;
                when generating =>
                    if to_integer(unsigned(N)) > num_generated then
                        if MODE = '0' then
                            if count > 15 then
                                count <= 0;
                            else
                                count <= count + 1;
                            end if;
                            reg <= values_4bit(count);
                        else
                            if count > 32 then
                                count <= 0;
                            else
                                count <= count + 1;
                            end if;
                            reg <= values_5bit(count);
                        end if;
                        num_generated <= num_generated + 1;
                    else
                        state <= waiting;
                    end if;
                when waiting =>
                    if wait_count < delay_cycles then
                        wait_count <= wait_count + 1;
                    else
                        STOPCU <= '1';
                        state <= IDLE;
                    end if;
                when others =>
                    state <= IDLE;
            end case;
        end if;
    end process;

    Q <= std_logic_vector(to_unsigned(reg, Q'length));
end Behavioral;

// VHDL entity LFSR_Translator, as the project stores it:
library IEEE;
use IEEE.STD_LOGIC_1164.ALL;
USE ieee.numeric_std.all;
use IEEE.STD_LOGIC_UNSIGNED.ALL;

entity LFSR_Translator is
    Port ( CLK : in STD_LOGIC;
           MODE : in STD_LOGIC;
           Q : in STD_LOGIC_VECTOR (4 downto 0);
           NQ : out STD_LOGIC_VECTOR (4 downto 0));
end LFSR_Translator;

architecture Behavioral of LFSR_Translator is
    -- Define lookup tables for 4-bit and 5-bit counters
    type lookup_array is array (0 to 31) of INTEGER;
    constant lookup_4bit : lookup_array := (
        0, 0, 5, 11, 14, 2, 3, 13, -- o to 7
        7, 9, 6, 10, 11, 5, 0, 0,-- 8 to  15
        0, 0, 0, 0, 0, 0, 0, 0,--16 to23
        0, 0, 0, 0, 0, 0, 0, 0--24 to 31
    );
    constant lookup_5bit : lookup_array := (
        0, 31, 11, 21, 15, 17, 24, 8, -- 0 to 7
        4, 28, 21, 11, 6, 26, 17, 15, -- 8 to  15
        23, 9, 20, 12, 30, 2, 3, 29, --16 to23
        7, 25, 26, 6, 13, 31, 0, 31 --24 to 31
    );

    signal counter : integer := 0;
    signal output_alternate : boolean := false;

begin
    -- Translate input Q to N= value based on the MODE input and alternate output values
    process(CLK)
        variable temp_N : INTEGER;
    begin
        if rising_edge(CLK) then
            if MODE = '0' then
                temp_N := lookup_4bit(to_integer(unsigned(Q)));
                if temp_N = 13 or temp_N = 5 or temp_N = 9 then
                    if output_alternate then
                        temp_N := temp_N - 1;
                    end if;
                    output_alternate <= not output_alternate;
                end if;
            else
                temp_N := lookup_5bit(to_integer(unsigned(Q)));
                if temp_N = 23 or temp_N = 19 or temp_N = 28 or temp_N = 17 or temp_N = 11 or temp_N = 6 or temp_N = 15 then
                    if output_alternate then
                        temp_N := temp_N - 1;
                    end if;
                    output_alternate <= not output_alternate;
                end if;
            end if;
            NQ <= std_logic_vector(to_unsigned(temp_N, 5));

            -- Update the counter for output alternation
            counter <= counter + 1;
            if counter = 1 then
                counter <= 0;
            end if;
        end if;
    end process;

end Behavioral;

// VHDL entity Seven_segment_LED_Display_Controller, as the project stores it:
library IEEE;
use IEEE.STD_LOGIC_1164.ALL;
use IEEE.STD_LOGIC_ARITH.ALL;
use IEEE.STD_LOGIC_UNSIGNED.ALL;

entity Seven_segment_LED_Display_Controller is
    Port (
        clock_100Mhz       : in  STD_LOGIC;
        reset              : in  STD_LOGIC;
        input_number       : in  STD_LOGIC_VECTOR(4 downto 0);
        Anode_Activate     : out STD_LOGIC_VECTOR(1 downto 0);
        LED_out            : out STD_LOGIC_VECTOR(6 downto 0)
    );
end Seven_segment_LED_Display_Controller;

architecture Behavioral of Seven_segment_LED_Display_Controller is
    signal LED_BCD                  : STD_LOGIC_VECTOR(3 downto 0);
    signal refresh_counter          : STD_LOGIC_VECTOR(17 downto 0) := (others => '0');
    signal LED_activating_counter   : STD_LOGIC := '0';

begin
    -- Refresh counter
    process (clock_100Mhz, reset)
    begin
        if reset = '1' then
            refresh_counter <= (others => '0');
        elsif rising_edge(clock_100Mhz) then
            refresh_counter <= refresh_counter + 1;
        end if;
    end process;

    LED_activating_counter <= refresh_counter(17);

    -- LED anode activating signals and BCD calculation
    process (LED_activating_counter, input_number)
    begin
        case LED_activating_counter is
            when '0' =>
                Anode_Activate <= "01";
                LED_BCD <= input_number(4 downto 3) & "00";
            when '1' =>
                Anode_Activate <= "10";
                LED_BCD <= input_number(2 downto 0) & "0";
            when others =>
                Anode_Activate <= "01";
                LED_BCD <= input_number(4 downto 3) & "00";
        end case;
    end process;

    -- LED cathode patterns
    process (LED_BCD)
    begin
        case LED_BCD is
            when "0000" => LED_out <= "0000001"; -- "0"
            when "0001" => LED_out <= "1001111"; -- "1"
            when "0010" => LED_out <= "0010010"; -- "2"
            when "0011" => LED_out <= "0000110"; -- "3"
            when "0100" => LED_out <= "1001100"; -- "4"
            when "0101" => LED_out <= "0100100"; -- "5"
            when "0110" => LED_out <= "0100000"; -- "6"
            when "0111" => LED_out <= "0001111"; -- "7"
            when "1000" => LED_out <= "0000000"; -- "8"
            when "1001" => LED_out <= "0000100"; -- "9"
            when others => LED_out <= "0000001"; -- "0"
        end case;
    end process;

end Behavioral;

// VHDL entity MainDesignLFSR, as the project stores it:
LIBRARY ieee;
USE ieee.std_logic_1164.all;

ENTITY MainDesignLFSR IS
  PORT (
    CLK: IN std_logic;
    START: IN std_logic;
    MODE: IN std_logic;
    RESET: IN std_logic;
    LENLOOP: IN std_logic;
    CATOD: out std_logic_vector(6 downto 0);
    ANOD: out std_logic_vector(3 downto 0)
  );
END ENTITY MainDesignLFSR;

    ARCHITECTURE Structural OF MainDesignLFSR IS
  SIGNAL clksgn200hz, LDCUsgn, RSTCU_lfsrsgn, looplenghtoutsgn, stoptocusgn: std_logic;
  signal NQsgn, Qsgn, Nsgn :std_logic_vector(4 downto 0);
  signal bcd_tens_1, bcd_units_0, bcd_tens_3, bcd_units_2: std_logic_vector (3 downto 0);

COMPONENT divisor_frecv200hz is
    Port (
        clk_in_100mhz : in  STD_LOGIC;
        clk_out_200hz: out STD_LOGIC
    );
end COMPONENT;


COMPONENT ControlUnit is
    Port (
        clkCU : in STD_LOGIC;
        RSTCU : in STD_LOGIC;
        STRTCU : in STD_LOGIC;
        STPCU : in STD_LOGIC;
        LDCU : out STD_LOGIC;
        RSTCU_lfsr : out STD_LOGIC
    );
end COMPONENT;
COMPONENT ButtonHandler IS
  PORT (
    clk: IN std_logic;
    reset: IN std_logic;
    button: IN std_logic;
    looplenghtout: OUT std_logic_vector(4 DOWNTO 0)
  );
END COMPONENT;


COMPONENT LFSR4_5bit is
    Port ( CLK : in  STD_LOGIC;
           RESET : in  STD_LOGIC;
           LOAD : in  STD_LOGIC;
           MODE : in  STD_LOGIC;
           N : out  STD_LOGIC_VECTOR (4 downto 0);
           Q : out  STD_LOGIC_VECTOR (4 downto 0);
           STOP : out STD_LOGIC
          );
end COMPONENT;

COMPONENT LFSR_translator is
    Port (
        CLKLFSRT : in STD_LOGIC;
        MODE : in STD_LOGIC;
        Q : in STD_LOGIC_VECTOR (4 downto 0);
        NQ : out STD_LOGIC_VECTOR (4 downto 0)
    );
end COMPONENT;

COMPONENT BinaryToBCD is
    Port (
        clk: IN std_logic;
        binary_input: IN std_logic_vector(4 DOWNTO 0);
    bcd_tens: OUT std_logic_vector(3 DOWNTO 0);
    bcd_units: OUT std_logic_vector(3 DOWNTO 0)

    );
end COMPONENT;

COMPONENT Display is
    Port (
        clk: in std_logic;
        looplen_unit: in std_logic_vector(3 downto 0);
        looplen_tens: in std_logic_vector(3 downto 0);
        lfsrout_unit: in std_logic_vector(3 downto 0);
        lfsrout_tens: in std_logic_vector(3 downto 0);
        cat: out std_logic_vector(6 downto 0);
        an: out std_logic_vector(3 downto 0)
    );
end COMPONENT;


BEGIN
    freq_div: divisor_frecv200hz
    port map (
        clk_in_100mhz => CLK,
        clk_out_200hz => clksgn200hz
     );

    -- Instantiate control unit
    CU_inst: ControlUnit
    PORT MAP (
     clkCU =>clksgn200hz,
       RSTCU => RESET,
       STRTCU => START,
       STPCU => stoptocusgn,
       LDCU => LDCUsgn,
       RSTCU_lfsr => RSTCU_lfsrsgn
    );

    BottonH_inst: ButtonHandler
    port map (
    clk => clksgn200hz,
        reset => RESET,
        button => LENLOOP,
        looplenghtout => Nsgn
            );

  -- Instantiate LFSR
  LFSR_inst: LFSR4_5bit
    PORT MAP (
             CLK => clksgn200hz,
           RESET => RSTCU_lfsrsgn,
           LOAD => LDCUsgn,
           MODE => MODE,
           N => Nsgn,
           Q => Qsgn,
           STOP => stoptocusgn
    );
    
    LFSRTinst: LFSR_translator
    port map (
        CLKLFSRT => clksgn200hz,
        MODE => MODE,
        Q => Qsgn,
        NQ => NQsgn
    );

BTBCB: BinaryToBCD
  PORT map(
    clk => clksgn200hz,
    binary_input => NQsgn,
    bcd_tens => bcd_tens_3,
    bcd_units => bcd_units_2
    );

BTBCB2: BinaryToBCD
  PORT map(
  clk => clksgn200hz,
    binary_input => NQsgn,
    bcd_tens => bcd_tens_1,
    bcd_units => bcd_units_0
    );
DCPLY: Display
    port map(
        clk => clksgn200hz,
        looplen_unit => bcd_units_0,
        looplen_tens => bcd_tens_1,
        lfsrout_unit => bcd_units_2,
        lfsrout_tens => bcd_tens_3,
        cat => CATOD,
        an => ANOD
    );

END ARCHITECTURE Structural;

// VHDL entity Display, as the project stores it:
library IEEE;
use IEEE.STD_LOGIC_1164.ALL;
use IEEE.STD_LOGIC_ARITH.ALL;
use IEEE.STD_LOGIC_UNSIGNED.ALL;

entity Display is
    Port (
        clk: in std_logic;
        looplen_unit: in std_logic_vector(3 downto 0);
        looplen_tens: in std_logic_vector(3 downto 0);
        lfsrout_unit: in std_logic_vector(3 downto 0);
        lfsrout_tens: in std_logic_vector(3 downto 0);
        cat: out std_logic_vector(6 downto 0);
        an: out std_logic_vector(3 downto 0)
    );
end Display;

architecture Behavioral of Display is
    signal counter: std_logic_vector(16 downto 0) := (others => '0');
    signal selection: std_logic_vector(1 downto 0);
    signal decoder: std_logic_vector(3 downto 0);
begin
    process(clk)
    begin
        if (rising_edge(clk)) then
            counter <= counter + 1;
        end if;
    end process;

    selection <= counter(16 downto 15);

    process(selection, looplen_unit, looplen_tens, lfsrout_unit, lfsrout_tens)
    begin
        if (selection = "00") then
            an <= "0001";
            decoder <= looplen_unit(3 downto 0);
        elsif (selection = "01") then
            an <= "0010";
            decoder <= looplen_tens(3 downto 0);
        elsif (selection = "10") then
            an <= "0100";
            decoder <= lfsrout_unit(3 downto 0);
        else
            an <= "1000";
            decoder <= lfsrout_tens(3 downto 0);
        end if;
    end process;

    process(decoder)
    begin
        case decoder is
            when "0000" => cat <= "1111110"; -- 0
            when "0001" => cat <= "0110000"; -- 1
            when "0010" => cat <= "1101101"; -- 2
            when "0011" => cat <= "1111001"; -- 3
            when "0100" => cat <= "0110011"; -- 4
            when "0101" => cat <= "1011011"; -- 5
            when "0110" => cat <= "1011111"; -- 6
            when "0111" => cat <= "1110000"; -- 7
            when "1000" => cat <= "1111111"; -- 8
            when "1001" => cat <= "1111011"; -- 9
            when others => cat <= "0000000"; -- Default case to handle other input values
        end case;
    end process;
end Behavioral;
